# Fritzing sketch Telkonet-OMNI (saved by Fritzing 0.9.6b)
breadboards: 1

parts:
  M1 = Humidity and Temperature Sensor DHT11
  R1 = PHOTOCELL [package=photocell]
  R2 = Resistor [tolerance=±5% resistance=220 package="2512 [SMD]"]
  Part1 = Arduino Uno (Rev3)
  Part2 = NeoPixel Stick [part_number=1426]
  S1 = Pushbutton [package="[THT]"]
  S2 = Pushbutton [package="[THT]"]
  S3 = Pushbutton [package="[THT]"]
  S4 = Pushbutton [package="[THT]"]
  S5 = Pushbutton [package="[THT]"]
  R3 = Resistor [tolerance=±5% resistance=220 package="0402 [SMD]"]
  R4 = Resistor [tolerance=±5% resistance=220 package="0402 [SMD]"]
  R5 = Resistor [tolerance=±5% resistance=220 package="0402 [SMD]"]
  R6 = Resistor [tolerance=±5% resistance=220 package="0402 [SMD]"]
  R7 = Resistor [tolerance=±5% resistance=220 package="0402 [SMD]"]
  BREAKOUT1 = ULN2003A breakout board
  MOTOR1 = 28BYJ-48 Stepper Motor
  J1 = Piezo Speaker

nets:
  +5V: M1.Vcc, R1.P$1, Part1.5V, Part2.+5V, S1.Pin_1, S1.Pin_2, S2.Pin_1, S2.Pin_2, S3.Pin_1, S3.Pin_2, S4.Pin_1, S4.Pin_2, S5.Pin_1, S5.Pin_2, BREAKOUT1.+5V
  N1: M1.Data, Part1.D2
  GND: M1.GND, R2.Pin_1, Part1.GND, Part2.GND, R3.Pin_1, BREAKOUT1.0V, J1.pin1
  N2: R1.P$2, R2.Pin_0, Part1.A0
  N3: Part1.A1, S1.Pin_3, S1.Pin_4, R7.Pin_0
  N4: Part1.D8, BREAKOUT1.In_4
  N5: Part1.D9_PWM, BREAKOUT1.In_3
  N6: Part1.D10_PWM/SS, BREAKOUT1.In_2
  N7: Part1.D11_PWM/MOSI, BREAKOUT1.In_1
  N8: Part1.D3_PWM, J1.pin2
  N9: Part1.D6_PWM, Part2.DATAOUT
  N10: S2.Pin_3, S2.Pin_4, R6.Pin_0, R7.Pin_1
  N11: S3.Pin_3, S3.Pin_4, R5.Pin_0, R6.Pin_1
  N12: S4.Pin_3, S4.Pin_4, R4.Pin_0, R5.Pin_1
  N13: S5.Pin_3, S5.Pin_4, R3.Pin_0, R4.Pin_1
  N14: BREAKOUT1.RED_wire, MOTOR1.RED
  N15: BREAKOUT1.ORANGE_wire, MOTOR1.ORANGE
  N16: BREAKOUT1.YELLOW_wire, MOTOR1.YELLOW
  N17: BREAKOUT1.PINK_wire, MOTOR1.PINK
  N18: BREAKOUT1.BLUE_wire, MOTOR1.BLUE

custom parts:
  Humidity and Temperature Sensor DHT11: Digital relative humidity & temperature sensor DHT11
  NeoPixel Stick: Make your own little LED strip arrangement with this stick of NeoPixel LEDs. We crammed 8 of the tiny 5050 (5mm x 5mm) smart RGB LEDs onto a PCB with mounting holes and a chainable design. Use only one microcontroller pin to control as many as you can chain together! Each LED is addressable as the driver chip is inside the LED. Each one has ~18mA constant current drive so the color will be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
  ULN2003A breakout board: ULN2003A 7-way Darlington Transistor Driver on breakoutboard
